# Fritzing sketch Circuitry (saved by Fritzing 0.9.6b)
breadboards: 1

parts:
  VCC1 = Battery block 9V
  M1 = RioRand LM2596
  U1 = SWITCH_SPDT [package=kps-1290]
  J1 = Basic Servo
  Q1 = MOSFET-NCHANNEL [package=to220v]
  M2 = DC Motor
  R1 = Resistor [tolerance=±5% resistance=10k package="0603 [SMD]"]
  R2 = Resistor [tolerance=±5% power=0.25 resistance=10 package=THT]
  D1 = Schottky Diode [part_number=1N5817 package="Melf DO-213 AB [SMD]"]
  Part1 = Arduino Ethernet Shield (Rev3)

nets:
  GND: VCC1.-, M1.Pin_2, M1.Pin_4, J1.gnd, Q1.S, R1.Pin_0, Part1.GND
  N1: VCC1.+, U1.P
  N2: M1.Pin_1, U1.O, Part1.VIN
  N3: M1.Pin_3, J1.vcc, M2.pin_2, D1.cathode
  N4: Q1.G, R1.Pin_1, R2.Pin_1
  N5: Q1.D, M2.pin_1, D1.anode
  N6: R2.Pin_0, Part1.PWM_D3
